// Logisim project clock.circ as structural Verilog: 1 circuit, main circuit main
module main (
);

  wire button_1_out, button_2_out, button_3_out, clock_1_out, counter_1_carry, counter_2_carry,
       counter_3_carry, counter_4_carry, counter_5_carry, or_1_out, or_2_out, or_3_out;
  wire [3:0] counter_1_q, counter_2_q, counter_3_q, counter_4_q, counter_5_q, counter_6_q;

  Clock clock_1 (.out(clock_1_out));
  Counter #(.max('h9), .trigger("falling"), .width(4)) counter_1 (
    .up(1'b1), .clk(or_1_out), .carry(counter_1_carry), .Q(counter_1_q));  // open: clr, load, count, D
  or or_1 (or_1_out, clock_1_out, button_3_out);
  Counter #(.max('h5), .trigger("falling"), .width(4)) counter_2 (
    .up(1'b1), .clk(counter_1_carry), .carry(counter_2_carry), .Q(counter_2_q));  // open: clr, load, count, D
  Hex_Digit_Display hex_digit_display_1 (.value(counter_6_q));  // open: dp
  Hex_Digit_Display hex_digit_display_2 (.value(counter_5_q));  // open: dp
  Button button_1 (.out(button_1_out));
  Hex_Digit_Display hex_digit_display_3 (.value(counter_4_q));  // open: dp
  Hex_Digit_Display hex_digit_display_4 (.value(counter_3_q));  // open: dp
  Button button_2 (.out(button_2_out));
  or or_2 (or_2_out, button_2_out, counter_2_carry);
  Hex_Digit_Display hex_digit_display_5 (.value(counter_2_q));  // open: dp
  Counter #(.max('h9), .trigger("falling"), .width(4)) counter_3 (
    .up(1'b1), .clk(or_2_out), .carry(counter_3_carry), .Q(counter_3_q));  // open: clr, load, count, D
  Hex_Digit_Display hex_digit_display_6 (.value(counter_1_q));  // open: dp
  Button button_3 (.out(button_3_out));
  Counter #(.max('h5), .trigger("falling"), .width(4)) counter_4 (
    .up(1'b1), .clk(counter_3_carry), .carry(counter_4_carry), .Q(counter_4_q));  // open: clr, load, count, D
  or or_3 (or_3_out, button_1_out, counter_4_carry);
  Counter #(.max('h9), .trigger("falling"), .width(4)) counter_5 (
    .up(1'b1), .clk(or_3_out), .carry(counter_5_carry), .Q(counter_5_q));  // open: clr, load, count, D
  Counter #(.max('h2), .trigger("falling"), .width(4)) counter_6 (
    .up(1'b1), .clk(counter_5_carry), .Q(counter_6_q));  // open: clr, load, count, D, carry
endmodule
